// Logisim project single-clock-mips.circ as structural Verilog: 7 circuits, main circuit main
module main (
);

  wire ALU_zero, ALUSrc, and_1_out, Branch, clock_1_out, jump, JumpRegister, link, MemRead, MemtoReg,
       MemWrite, RegDst, RegWrite;
  wire [3:0] ALUOp;
  wire [4:0] Instr__Splitter_rd, Instr__Splitter_rs, Instr__Splitter_rt, multiplexer_5_out,
       multiplexer_7_out, shamt;
  wire [5:0] func, opcode;
  wire [15:0] Instr__Splitter_immediate;
  wire [25:0] j_format;
  wire [27:0] adder_1_out, bit_extender_1_out, shifter_1_out;
  wire [31:0] adder_2_out, ALU_result, bit_extender_2_out, Data_Mem_read_data, Instr__Mem_read_data,
       multiplexer_1_out, multiplexer_2_out, multiplexer_3_out, multiplexer_4_out, multiplexer_6_out,
       multiplexer_8_out, PC_q, R1, Regs_r2, shifter_2_out;
  wire [31:28] adder_1_out_2;

  assign bit_extender_1_out = {{2{1'b0}}, j_format};  // Bit_Extender bit_extender_1
  Multiplexer #(.width(32), .enable("false")) multiplexer_1 (
    .in0(multiplexer_2_out), .in1({adder_1_out_2, shifter_1_out}), .out(multiplexer_1_out), .sel(jump));
  Clock clock_1 (.out(clock_1_out));
  Shifter #(.width(28)) shifter_1 (.in(bit_extender_1_out), .\dist (5'b00010), .out(shifter_1_out));
  Register #(.width(32)) PC (.D(multiplexer_1_out), .en(1'b1), .Q(PC_q), .clk(clock_1_out), .clr(1'b0));
  Multiplexer #(.width(32), .enable("false")) multiplexer_2 (
    .in0(multiplexer_3_out), .in1(adder_2_out), .out(multiplexer_2_out), .sel(and_1_out));
  Adder #(.width(32)) adder_1 (.a(32'h4), .b(PC_q), .out({adder_1_out_2, adder_1_out}), .cin(1'b0));  // open: cout
  Instruction_Memory Instr__Mem (
    .Address(PC_q), .MemWrite(1'b0), .MemRead(1'b1), .Read_Data(Instr__Mem_read_data));  // open: Write_Data
  Multiplexer #(.width(32), .enable("false")) multiplexer_3 (
    .in0({adder_1_out_2, adder_1_out}), .in1(R1), .out(multiplexer_3_out), .sel(JumpRegister));
  Instruction_splitter Instr__Splitter (
    .Instruction_Code(Instr__Mem_read_data), .j_format(j_format), .Immediate(Instr__Splitter_immediate),
    .Func(func), .Shamt(shamt), .rd(Instr__Splitter_rd), .rt(Instr__Splitter_rt), .rs(Instr__Splitter_rs),
    .Opcode(opcode));
  Control Control (
    .func(func), .opcode(opcode), .ALUOp(ALUOp), .ALUSrc(ALUSrc), .RegDst(RegDst), .MemRead(MemRead),
    .MemWrite(MemWrite), .MemtoReg(MemtoReg), .Branch(Branch), .RegWrite(RegWrite), .jump(jump), .link(link),
    .JumpRegister(JumpRegister));
  assign bit_extender_2_out = {{16{Instr__Splitter_immediate[15]}}, Instr__Splitter_immediate};  // Bit_Extender bit_extender_2
  Shifter #(.width(32)) shifter_2 (.in(bit_extender_2_out), .\dist (5'b00010), .out(shifter_2_out));
  and and_1 (and_1_out, Branch, ALU_zero);
  Adder #(.width(32)) adder_2 (
    .a({adder_1_out_2, adder_1_out}), .b(shifter_2_out), .out(adder_2_out), .cin(1'b0));  // open: cout
  Multiplexer #(.width(32), .enable("false")) multiplexer_4 (
    .in0(multiplexer_6_out), .in1({adder_1_out_2, adder_1_out}), .out(multiplexer_4_out), .sel(link));
  Multiplexer #(.width(5), .enable("false")) multiplexer_5 (
    .in0(Instr__Splitter_rd), .in1(Instr__Splitter_rt), .out(multiplexer_5_out), .sel(RegDst));
  Multiplexer #(.width(32), .enable("false")) multiplexer_6 (
    .in0(ALU_result), .in1(Data_Mem_read_data), .out(multiplexer_6_out), .sel(MemtoReg));
  Multiplexer #(.width(5), .enable("false")) multiplexer_7 (
    .in0(multiplexer_5_out), .in1({5{1'b1}}), .out(multiplexer_7_out), .sel(link));
  Register_Bank Regs (
    .RegWr(RegWrite), .AW(multiplexer_7_out), .Data_In(multiplexer_4_out), .AR1(Instr__Splitter_rs),
    .AR2(Instr__Splitter_rt), .R1(R1), .R2(Regs_r2));
  Multiplexer #(.width(32), .enable("false")) multiplexer_8 (
    .in0(Regs_r2), .in1(bit_extender_2_out), .out(multiplexer_8_out), .sel(ALUSrc));
  ALU ALU (.ALUCtrl(ALUOp), .R1(R1), .R2(multiplexer_8_out), .Result(ALU_result), .Zero(ALU_zero));
  Data_Memory Data_Mem (
    .Address(ALU_result), .Write_Data(Regs_r2), .MemWrite(MemWrite), .MemRead(MemRead),
    .Read_Data(Data_Mem_read_data));
endmodule

module Register_Bank (
  input  RegWr,
  input  [4:0] AW,
  input  [31:0] Data_In,
  input  [4:0] AR1,
  input  [4:0] AR2,
  output [31:0] R1,
  output [31:0] R2
);

  wire clock_1_out, clock_2_out, clock_3_out, clock_4_out, clock_5_out, clock_6_out, clock_7_out,
       clock_8_out, clock_9_out, clock_10_out, clock_11_out, clock_12_out, clock_13_out, clock_14_out,
       clock_15_out, clock_16_out, clock_17_out, clock_18_out, clock_19_out, clock_20_out, clock_21_out,
       clock_22_out, clock_23_out, clock_24_out, clock_25_out, clock_26_out, clock_27_out, clock_28_out,
       clock_29_out, clock_30_out, clock_31_out;
  wire [3:0] decoder_1_out0, decoder_1_out4, decoder_1_out8, decoder_1_out12, decoder_1_out16,
       decoder_1_out20, decoder_1_out24, decoder_1_out28;
  wire [31:0] o1, o2, o3, o4, o5, o6, o7, o8, o9, o10, o11, o12, o13, o14, o15, o16, o17, o18, o19, o20, o21,
       o22, o23, o24, o25, o26, o27, o28, o29, o30, o31;

  Clock clock_1 (.out(clock_1_out));
  Clock clock_2 (.out(clock_2_out));
  Clock clock_3 (.out(clock_3_out));
  Register #(.width(32)) u_r1 (.D(Data_In), .en(decoder_1_out0[1]), .Q(o1), .clk(clock_1_out), .clr(1'b0));
  Register #(.width(32)) u_r2 (.D(Data_In), .en(decoder_1_out0[2]), .Q(o2), .clk(clock_2_out), .clr(1'b0));
  Register #(.width(32)) r3 (.D(Data_In), .en(decoder_1_out0[3]), .Q(o3), .clk(clock_3_out), .clr(1'b0));
  Clock clock_4 (.out(clock_4_out));
  Clock clock_5 (.out(clock_5_out));
  Clock clock_6 (.out(clock_6_out));
  Clock clock_7 (.out(clock_7_out));
  Multiplexer #(.select(5), .width(32), .enable("false")) multiplexer_1 (
    .in0({32{1'b0}}), .in1(o1), .in2(o2), .in3(o3), .in4(o4), .in5(o5), .in6(o6), .in7(o7), .in8(o8),
    .in9(o9), .in10(o10), .in11(o11), .in12(o12), .in13(o13), .in14(o14), .in15(o15), .in16(o16), .in17(o17),
    .in18(o18), .in19(o19), .in20(o20), .in21(o21), .in22(o22), .in23(o23), .in24(o24), .in25(o25),
    .in26(o26), .in27(o27), .in28(o28), .in29(o29), .in30(o30), .in31(o31), .out(R1), .sel(AR1));
  Register #(.width(32)) r4 (.D(Data_In), .en(decoder_1_out4[0]), .Q(o4), .clk(clock_4_out), .clr(1'b0));
  Register #(.width(32)) r5 (.D(Data_In), .en(decoder_1_out4[1]), .Q(o5), .clk(clock_5_out), .clr(1'b0));
  Register #(.width(32)) r6 (.D(Data_In), .en(decoder_1_out4[2]), .Q(o6), .clk(clock_6_out), .clr(1'b0));
  Register #(.width(32)) r7 (.D(Data_In), .en(decoder_1_out4[3]), .Q(o7), .clk(clock_7_out), .clr(1'b0));
  Decoder #(.select(5), .disabled(0)) decoder_1 (
    .out0(decoder_1_out0[0]), .out1(decoder_1_out0[1]), .out2(decoder_1_out0[2]), .out3(decoder_1_out0[3]),
    .out4(decoder_1_out4[0]), .out5(decoder_1_out4[1]), .out6(decoder_1_out4[2]), .out7(decoder_1_out4[3]),
    .out8(decoder_1_out8[0]), .out9(decoder_1_out8[1]), .out10(decoder_1_out8[2]), .out11(decoder_1_out8[3]),
    .out12(decoder_1_out12[0]), .out13(decoder_1_out12[1]), .out14(decoder_1_out12[2]),
    .out15(decoder_1_out12[3]), .out16(decoder_1_out16[0]), .out17(decoder_1_out16[1]),
    .out18(decoder_1_out16[2]), .out19(decoder_1_out16[3]), .out20(decoder_1_out20[0]),
    .out21(decoder_1_out20[1]), .out22(decoder_1_out20[2]), .out23(decoder_1_out20[3]),
    .out24(decoder_1_out24[0]), .out25(decoder_1_out24[1]), .out26(decoder_1_out24[2]),
    .out27(decoder_1_out24[3]), .out28(decoder_1_out28[0]), .out29(decoder_1_out28[1]),
    .out30(decoder_1_out28[2]), .out31(decoder_1_out28[3]), .sel(AW), .en(RegWr));
  Clock clock_8 (.out(clock_8_out));
  Clock clock_9 (.out(clock_9_out));
  Clock clock_10 (.out(clock_10_out));
  Clock clock_11 (.out(clock_11_out));
  Register #(.width(32)) r8 (.D(Data_In), .en(decoder_1_out8[0]), .Q(o8), .clk(clock_8_out), .clr(1'b0));
  Register #(.width(32)) r9 (.D(Data_In), .en(decoder_1_out8[1]), .Q(o9), .clk(clock_9_out), .clr(1'b0));
  Register #(.width(32)) r10 (.D(Data_In), .en(decoder_1_out8[2]), .Q(o10), .clk(clock_10_out), .clr(1'b0));
  Register #(.width(32)) r11 (.D(Data_In), .en(decoder_1_out8[3]), .Q(o11), .clk(clock_11_out), .clr(1'b0));
  Clock clock_12 (.out(clock_12_out));
  Clock clock_13 (.out(clock_13_out));
  Clock clock_14 (.out(clock_14_out));
  Clock clock_15 (.out(clock_15_out));
  Register #(.width(32)) r12 (.D(Data_In), .en(decoder_1_out12[0]), .Q(o12), .clk(clock_12_out), .clr(1'b0));
  Register #(.width(32)) r13 (.D(Data_In), .en(decoder_1_out12[1]), .Q(o13), .clk(clock_13_out), .clr(1'b0));
  Register #(.width(32)) r14 (.D(Data_In), .en(decoder_1_out12[2]), .Q(o14), .clk(clock_14_out), .clr(1'b0));
  Register #(.width(32)) r15 (.D(Data_In), .en(decoder_1_out12[3]), .Q(o15), .clk(clock_15_out), .clr(1'b0));
  Clock clock_16 (.out(clock_16_out));
  Clock clock_17 (.out(clock_17_out));
  Clock clock_18 (.out(clock_18_out));
  Clock clock_19 (.out(clock_19_out));
  Register #(.width(32)) r16 (.D(Data_In), .en(decoder_1_out16[0]), .Q(o16), .clk(clock_16_out), .clr(1'b0));
  Register #(.width(32)) r17 (.D(Data_In), .en(decoder_1_out16[1]), .Q(o17), .clk(clock_17_out), .clr(1'b0));
  Register #(.width(32)) r18 (.D(Data_In), .en(decoder_1_out16[2]), .Q(o18), .clk(clock_18_out), .clr(1'b0));
  Register #(.width(32)) r19 (.D(Data_In), .en(decoder_1_out16[3]), .Q(o19), .clk(clock_19_out), .clr(1'b0));
  Register #(.width(32)) r20 (.D(Data_In), .en(decoder_1_out20[0]), .Q(o20), .clk(clock_20_out), .clr(1'b0));
  Clock clock_20 (.out(clock_20_out));
  Register #(.width(32)) r21 (.D(Data_In), .en(decoder_1_out20[1]), .Q(o21), .clk(clock_21_out), .clr(1'b0));
  Clock clock_21 (.out(clock_21_out));
  Register #(.width(32)) r22 (.D(Data_In), .en(decoder_1_out20[2]), .Q(o22), .clk(clock_22_out), .clr(1'b0));
  Clock clock_22 (.out(clock_22_out));
  Register #(.width(32)) r23 (.D(Data_In), .en(decoder_1_out20[3]), .Q(o23), .clk(clock_23_out), .clr(1'b0));
  Clock clock_23 (.out(clock_23_out));
  Register #(.width(32)) r24 (.D(Data_In), .en(decoder_1_out24[0]), .Q(o24), .clk(clock_24_out), .clr(1'b0));
  Clock clock_24 (.out(clock_24_out));
  Register #(.width(32)) r25 (.D(Data_In), .en(decoder_1_out24[1]), .Q(o25), .clk(clock_25_out), .clr(1'b0));
  Clock clock_25 (.out(clock_25_out));
  Register #(.width(32)) r26 (.D(Data_In), .en(decoder_1_out24[2]), .Q(o26), .clk(clock_26_out), .clr(1'b0));
  Clock clock_26 (.out(clock_26_out));
  Register #(.width(32)) r27 (.D(Data_In), .en(decoder_1_out24[3]), .Q(o27), .clk(clock_27_out), .clr(1'b0));
  Clock clock_27 (.out(clock_27_out));
  Multiplexer #(.select(5), .width(32), .enable("false")) multiplexer_2 (
    .in0({32{1'b0}}), .in1(o1), .in2(o2), .in3(o3), .in4(o4), .in5(o5), .in6(o6), .in7(o7), .in8(o8),
    .in9(o9), .in10(o10), .in11(o11), .in12(o12), .in13(o13), .in14(o14), .in15(o15), .in16(o16), .in17(o17),
    .in18(o18), .in19(o19), .in20(o20), .in21(o21), .in22(o22), .in23(o23), .in24(o24), .in25(o25),
    .in26(o26), .in27(o27), .in28(o28), .in29(o29), .in30(o30), .in31(o31), .out(R2), .sel(AR2));
  Register #(.width(32)) r28 (.D(Data_In), .en(decoder_1_out28[0]), .Q(o28), .clk(clock_28_out), .clr(1'b0));
  Clock clock_28 (.out(clock_28_out));
  Register #(.width(32)) r29 (.D(Data_In), .en(decoder_1_out28[1]), .Q(o29), .clk(clock_29_out), .clr(1'b0));
  Clock clock_29 (.out(clock_29_out));
  Register #(.width(32)) r30 (.D(Data_In), .en(decoder_1_out28[2]), .Q(o30), .clk(clock_30_out), .clr(1'b0));
  Clock clock_30 (.out(clock_30_out));
  Register #(.width(32)) r31 (.D(Data_In), .en(decoder_1_out28[3]), .Q(o31), .clk(clock_31_out), .clr(1'b0));
  Clock clock_31 (.out(clock_31_out));

  // Other names for the same wires on the sheet: DI[31:0] = Data_In

  // Notes on the sheet:
  //   r0
endmodule

module ALU (
  input  [3:0] ALUCtrl,
  input  [31:0] R1,
  input  [31:0] R2,
  output [31:0] Result,
  output Zero
);

  wire [0:0] comparator_1_lt;
  wire [31:0] adder_1_out, and_1_out, nor_1_out, or_1_out, subtractor_1_out;

  assign and_1_out = R1 & R2;  // AND_Gate and_1, 32 bits wide
  assign or_1_out = R1 | R2;  // OR_Gate or_1, 32 bits wide
  Adder #(.width(32)) adder_1 (.a(R1), .b(R2), .out(adder_1_out), .cin(1'b0));  // open: cout
  Subtractor #(.width(32)) subtractor_1 (.a(R1), .b(R2), .out(subtractor_1_out), .bin(1'b0));  // open: bout
  assign nor_1_out = ~(R1 | R2);  // NOR_Gate nor_1, 32 bits wide
  Comparator #(.width(32)) comparator_1 (.a(R1), .b(R2), .lt(comparator_1_lt[0]));  // open: gt, eq
  Multiplexer #(.select(4), .width(32), .enable("false")) multiplexer_1 (
    .in0(and_1_out), .in1(or_1_out), .in2(adder_1_out), .in6(subtractor_1_out),
    .in7({{31{1'b0}}, comparator_1_lt[0]}), .in12(nor_1_out), .out(Result), .sel(ALUCtrl));  // open: in3, in4, in5, in8, in9, in10, in11, in13, in14, in15
  nor nor_2 (Zero, Result[0], Result[1], Result[2], Result[3], Result[4], Result[5], Result[6], Result[7], Result[8], Result[9], Result[10], Result[11], Result[12], Result[13], Result[14], Result[16], Result[17], Result[18], Result[19], Result[20], Result[21], Result[22], Result[23], Result[24], Result[25], Result[26], Result[27], Result[28], Result[29], Result[30], Result[31]);

  // Notes on the sheet:
  //   0000 (0) = AND
  //   0001 (1) = OR
  //   0010 (2) = Add
  //   0110 (6) = Sub
  //   0111 (7) = SLT (<)
  //   1100 (12) = NOR
endmodule

module Instruction_Memory (
  input  [31:0] Address,
  input  [31:0] Write_Data,
  input  MemWrite,
  input  MemRead,
  output [31:0] Read_Data
);

  wire clock_1_out;
  wire [31:0] shifter_1_out;

  Shifter #(.width(32), .shift("lr")) shifter_1 (.in(Address), .\dist (5'b00010), .out(shifter_1_out));
  Clock clock_1 (.out(clock_1_out));
  RAM #(.dataWidth(32), .bus("separate")) ram_1 (
    .addr(shifter_1_out[7:0]), .din(Write_Data), .data(Read_Data), .str(MemWrite), .sel(1'b1),
    .clk(clock_1_out), .ld(MemRead), .clr(1'b0));
endmodule

module Instruction_splitter (
  input  [31:0] Instruction_Code,
  output [25:0] j_format,
  output [15:0] Immediate,
  output [5:0] Func,
  output [4:0] Shamt,
  output [4:0] rd,
  output [4:0] rt,
  output [4:0] rs,
  output [5:0] Opcode
);


  assign Func = Instruction_Code[5:0];
  assign Immediate = Instruction_Code[15:0];
  assign j_format = Instruction_Code[25:0];
  assign Opcode = Instruction_Code[31:26];
  assign rd = Instruction_Code[15:11];
  assign rs = Instruction_Code[25:21];
  assign rt = Instruction_Code[20:16];
  assign Shamt = Instruction_Code[10:6];

  // Notes on the sheet:
  //   I-Format
  //   R-format
endmodule

module Control (
  input  [5:0] func,
  input  [5:0] opcode,
  output [3:0] ALUOp,
  output ALUSrc,
  output RegDst,
  output MemRead,
  output MemWrite,
  output MemtoReg,
  output Branch,
  output RegWrite,
  output jump,
  output link,
  output JumpRegister
);

  wire add, addu, \and , and_1_out, and_2_out, arith, CP0_Instr, j, \nor , not_1_out, \or , or_1_out,
       or_2_out, or_3_out, sll, slt, sltu, sub, subu, syscall, \xor ;

  Decoder #(.select(5), .disabled(0)) decoder_1 (
    .out0(arith), .out2(j), .out3(link), .out4(Branch), .out16(CP0_Instr), .sel(opcode[4:0]), .en(not_1_out));  // open: out1, out5, out6, out7, out8, out9, out10, out11, out12, out13, out14, out15, out17, out18, out19, out20, out21, out22, out23, out24, out25, out26, out27, out28, out29, out30, out31
  not not_1 (not_1_out, opcode[5]);
  Decoder #(.select(5), .disabled(0)) decoder_2 (
    .out3(MemRead), .out11(MemWrite), .sel(opcode[4:0]), .en(opcode[5]));  // open: out0, out1, out2, out4, out5, out6, out7, out8, out9, out10, out12, out13, out14, out15, out16, out17, out18, out19, out20, out21, out22, out23, out24, out25, out26, out27, out28, out29, out30, out31
  and and_1 (and_1_out, arith, ~func[5]);  // AND_Gate
  and and_2 (and_2_out, arith, func[5]);
  Decoder #(.select(5), .disabled(0)) decoder_3 (
    .out0(sll), .out8(JumpRegister), .out12(syscall), .sel(func[4:0]), .en(and_1_out));  // open: out1, out2, out3, out4, out5, out6, out7, out9, out10, out11, out13, out14, out15, out16, out17, out18, out19, out20, out21, out22, out23, out24, out25, out26, out27, out28, out29, out30, out31
  Decoder #(.select(5), .disabled(0)) decoder_4 (
    .out0(add), .out1(addu), .out2(sub), .out3(subu), .out4(\and ), .out5(\or ), .out6(\xor ), .out7(\nor ),
    .out10(slt), .out11(sltu), .sel(func[4:0]), .en(and_2_out));  // open: out8, out9, out12, out13, out14, out15, out16, out17, out18, out19, out20, out21, out22, out23, out24, out25, out26, out27, out28, out29, out30, out31
  or or_1 (or_1_out, MemWrite, addu, add, MemRead);
  or or_2 (or_2_out, subu, sub, Branch);
  or or_3 (or_3_out, sltu, slt);
  or or_4 (ALUOp[0], \or , or_3_out, 1'b0);
  or or_5 (ALUOp[1], or_1_out, or_2_out, or_3_out, 1'b0);
  or or_6 (ALUOp[2], or_2_out, \nor , or_3_out, 1'b0);
  or or_7 (ALUOp[3], \nor , 1'b0);
  or or_8 (ALUSrc, JumpRegister, MemRead, MemWrite);
  buf or_9 (RegDst, MemRead);  // OR_Gate
  or or_10 (RegWrite, MemRead, add, addu, sub, subu, \and , \or , \xor , \nor , link, slt, sltu);
  or or_11 (jump, j, link);

  assign MemtoReg = MemRead;

  // Other names for the same wires on the sheet: beq = Branch; jal = link; jr = JumpRegister; lw = MemRead;
  //   sw = MemWrite

  // Notes on the sheet:
  //   opcode
  //   func
endmodule

module Data_Memory (
  input  [31:0] Address,
  input  [31:0] Write_Data,
  input  MemWrite,
  input  MemRead,
  output [31:0] Read_Data
);

  wire clock_1_out;
  wire [31:0] shifter_1_out;

  Shifter #(.width(32), .shift("lr")) shifter_1 (.in(Address), .\dist (5'b00010), .out(shifter_1_out));
  Clock clock_1 (.out(clock_1_out));
  RAM #(.dataWidth(32), .bus("separate")) ram_1 (
    .addr(shifter_1_out[7:0]), .din(Write_Data), .data(Read_Data), .str(MemWrite), .sel(1'b1),
    .clk(clock_1_out), .ld(MemRead), .clr(1'b0));
endmodule
